# Fritzing sketch FOR-TC-OC-Ver1 (saved by Fritzing 1.0.6)
circuit board: 8.46667cm x 5.64444cm
breadboards: 1

parts:
  TP1 = mystery part, 4 pins [chip_label=TC_TP]
  R1 = Resistor [tolerance=±5% power=0.25W resistance=100k package=THT]
  R2 = Resistor [tolerance=±5% power=0.25W resistance=15k package=THT]
  R3 = Resistor [tolerance=±5% power=0.25W resistance=2.2k package=THT]
  D1-BAT43 = Rectifier Diode [part_number=BAT43 package="300 mil [THT]"]
  D2-BAT43 = Rectifier Diode [part_number=BAT43 package="300 mil [THT]"]
  R4 = Resistor [tolerance=±5% power=0.25W resistance=330 package=THT]
  R5 = Resistor [tolerance=±5% power=0.25W resistance=100k package=THT]
  TP2 = mystery part, 4 pins [chip_label=ESP32_TP]
  Q1-2N7000 = MOSFET-NCHANNEL [package=to220v]
  XIXO_ESP32-S4 = IC, DIP package, 14 pins [chip_label="XIXO ESP32-S3"]

nets:
  N1: TP1.pin1, R2.Pin_0, R5.Pin_1, Q1-2N7000.S
  N2: TP1.pin4, R1.Pin_0, Q1-2N7000.D
  N3: R1.Pin_1, R2.Pin_1, R3.Pin_0
  N4: R3.Pin_1, D1-BAT43.cathode, D2-BAT43.anode, TP2.pin1, XIXO_ESP32-S4.pin2
  N5: D1-BAT43.anode, TP2.pin2, XIXO_ESP32-S4.pin13
  N6: D2-BAT43.cathode, TP2.pin3, XIXO_ESP32-S4.pin12
  N7: R4.Pin_0, TP2.pin4, XIXO_ESP32-S4.pin1
  N8: R4.Pin_1, R5.Pin_0, Q1-2N7000.G

notes:
  SIG       GND
  TX 3V GND RX
  43 6  5  4  3  2  1
  44 7  8  9 3v3 G 5v
